# Fritzing sketch 2buttons gate sketch (saved by Fritzing 0.8.3b)
breadboards: 1

parts:
  Part1 = Arduino Uno (Rev3)
  S1 = Pushbutton [package="[THT]"]
  S2 = Pushbutton [package="[THT]"]
  LED1 = LED - 5mm [color="Red (633nm)" package="5 mm [THT]"]
  R3 = Resistor [package="2010 [SMD]"]  # not connected

nets:
  N1: Part1.GND, S1.Pin_1, S1.Pin_2, S2.Pin_1, S2.Pin_2
  N2: Part1.D13/SCK, LED1.cathode
  N3: Part1.D2, S2.Pin_3, S2.Pin_4
  N4: Part1.D4, S1.Pin_3, S1.Pin_4
